// Digital circuit Computer.dig as structural Verilog
module Computer (
  input  clk
);

  wire _7485_2_pin2, _7485_2_pin3, _7485_2_pin4, _74157_1_pin15, _74157_2_pin15, _74157_7_pin15,
       _74157_8_pin15, _74161_4_pin7, _74161_4_pin10, _74245_1_pin1, _74245_2_pin1, _74245_3_pin1,
       _74245_5_pin1, _74245_6_pin1, _74245_7_pin1, _74245_7_pin11, _74245_7_pin12, _74245_7_pin13,
       _74245_7_pin14, _74245_7_pin15, _74245_7_pin16, _74245_7_pin17, _74245_8_pin1, _74260_1_pin4,
       _74260_1_pin8, _74260_1_pin9, _74260_1_pin10, _74260_1_pin11, _74373_3_pin1, _74373_4_pin1, AB0, AB1,
       AB2, AB3, AB4, AB5, AB6, AB7, AB8, AB9, AB10, AB11, AB12, AB13, AB14, AB15, ABHtoDB, ABLtoDB, ADD_SUB,
       ADDER, AND0, AND1, AND2, AND3, AND4, AND5, AND6, AND7, and_2_out, and_3_out, AND_OR, ANDOR0, ANDOR1,
       ANDOR2, ANDOR3, ANDOR4, ANDOR5, ANDOR6, ANDOR7, AV, B0, B1, B2, B3, B4, B5, B6, B7, B_eq, B_gt, B_IMM,
       B_lt, B_WE, BEQ, BGT, BLT, BtoDB, button_1_out, button_2_out, button_3_out, Byte_1_p24, Byte_1_p30,
       Byte_2_p19, Byte_2_p25, Byte_3_p19, Byte_4_p11, CF, CF_BF, CFlag, CLK_t, CLR, CLR_CF_BF, CMP_eq,
       CMP_gt, CMP_lt, CO_CI, DB0, DB1, DB2, DB3, DB4, DB5, DB6, DB7, EP0, EP1, EP2, EP3, EP4, EP5, EP6, EP7,
       EP_DIR, EP_OE, EPS, eq, gt, HALT, iAB_MAR, JCF, JMP, LD, LOG0, LOG1, LOG2, LOG3, LOG4, LOG5, LOG6,
       LOG7, LOGIC, lt, MAR0, MAR1, MAR2, MAR3, MAR4, MAR5, MAR6, MAR7, MAR8, MAR9, MAR10, MAR11, MAR12,
       MAR13, MAR14, MAR15, MAR_AB_DB, MAR_WHI, MAR_WLO, not_18_out, not_19_out, not_20_out, OPC0, OPC1,
       OPC2, OPC3, OPC5, OR0, OR1, OR2, OR3, OR4, OR5, OR6, OR7, or_1_out, or_2_out, P1_LOGIC, PC0, PC1, PC2,
       PC3, PC4, PC5, PC6, PC7, PC8, PC9, PC10, PC11, PC12, PC13, PC14, PC15, pulldown_1_out, pulldown_2_out,
       pulldown_3_out, pulldown_5_out, pulldown_14_out, pulldown_15_out, pulldown_16_out, pulldown_17_out,
       pulldown_26_out, pulldown_27_out, pulldown_36_out, pulldown_37_out, pulldown_48_out, pulldown_49_out,
       pulldown_50_out, pulldown_51_out, R0, R1, R2, R3, R4, R5, R6, R7, R_RE, R_WE, RAM_CE, RAM_RE, RAM_WE,
       RESET, rs_ff_as_1_nq, rs_ff_as_1_q, SUM0, SUM1, SUM2, SUM3, SUM4, SUM5, SUM6, SUM7, TIE0, TIE1, TIE2,
       XOR0, XOR1, XOR2, XOR3, XOR4, XOR5, XOR6, XOR7, xor_1_out, XOR_P1, XORB0, XORB1, XORB2, XORB3, XORB4,
       XORB5, XORB6, XORB7;
  wire [3:0] lookuptable_1_out, lookuptable_2_out, lookuptable_3_out, lookuptable_4_out, lookuptable_5_out,
       lookuptable_6_out, lookuptable_7_out, lookuptable_8_out;
  wire [9:0] lookuptable_9_out, lookuptable_11_out, lookuptable_12_out;
  wire [9:5] lookuptable_10_out;
  wire [15:8] keyboard_1_d;

  // _28c512 Byte_4: pin names not known; wires that end beside it: PC15, PC12, PC7, PC6, PC5, PC4, PC3, PC2, PC1, 1'b1, Byte_4_p11, PC14, PC13, PC8, PC9, PC11, iAB_MAR, PC10
  // _28c512 Byte_3: pin names not known; wires that end beside it: PC0, AB8, AB9, AB10, 1'b0, PC15, PC12, PC7, PC6, PC5, PC4, PC3, PC2, PC1, AB13, AB12, AB11, 1'b1, Byte_3_p19, PC14, PC13, PC8, PC9, PC11, iAB_MAR, PC10
  // _28c512 Byte_2: pin names not known; wires that end beside it: PC0, AB0, AB1, AB2, 1'b0, PC15, PC12, PC7, PC6, PC5, PC4, PC3, PC2, PC1, AB5, AB4, AB3, 1'b1, Byte_2_p19, PC14, PC13, PC8, PC9, PC11, Byte_2_p25, PC10
  // _28c512 Byte_1: pin names not known; wires that end beside it: PC0, B0, B1, B2, 1'b0, PC15, PC12, PC7, PC6, PC5, PC4, PC3, PC2, PC1, PC0, OPC0, OPC1, OPC2, 1'b0, B5, B4, B3, 1'b1, Byte_1_p24, PC14, PC13, PC8, PC9, PC11, Byte_1_p30, PC10
  PullUp pullup_1 (.out(Byte_4_p11));
  PullDown pulldown_1 (.out(pulldown_1_out));
  PullUp pullup_2 (.out(Byte_3_p19));
  PullDown pulldown_2 (.out(pulldown_2_out));
  PullUp pullup_3 (.out(Byte_2_p19));
  not not_1 (Byte_2_p25, B_IMM);
  PullDown pulldown_3 (.out(pulldown_3_out));
  PullUp pullup_4 (.out(Byte_1_p24));
  PullDown pulldown_4 (.out(Byte_1_p30));
  PullDown pulldown_5 (.out(pulldown_5_out));
  PullDown pulldown_6 (.out(ANDOR7));
  PullDown pulldown_7 (.out(ANDOR6));
  PullDown pulldown_8 (.out(ANDOR5));
  PullDown pulldown_9 (.out(ANDOR4));
  PullDown pulldown_10 (.out(ANDOR3));
  PullDown pulldown_11 (.out(ANDOR2));
  PullDown pulldown_12 (.out(ANDOR1));
  PullDown pulldown_13 (.out(ANDOR0));
  Seven_Seg_Hex seven_seg_hex_1 (.d(lookuptable_1_out), .dp(pulldown_14_out));
  LookUpTable #(.Bits(4)) lookuptable_1 (.in0(AB12), .in1(AB13), .in2(AB14), .in3(AB15), .out(lookuptable_1_out));
  Seven_Seg_Hex seven_seg_hex_2 (.d(lookuptable_2_out), .dp(pulldown_15_out));
  LookUpTable #(.Bits(4)) lookuptable_2 (.in0(PC12), .in1(PC13), .in2(PC14), .in3(PC15), .out(lookuptable_2_out));
  PullDown pulldown_14 (.out(pulldown_14_out));
  PullDown pulldown_15 (.out(pulldown_15_out));
  LED led_1 (.in(DB7));
  LED led_2 (.in(DB6));
  LED led_3 (.in(R7));
  LED led_4 (.in(R6));
  Seven_Seg_Hex seven_seg_hex_3 (.d(lookuptable_3_out), .dp(pulldown_16_out));
  PullDown pulldown_16 (.out(pulldown_16_out));
  LookUpTable #(.Bits(4)) lookuptable_3 (.in0(AB8), .in1(AB9), .in2(AB10), .in3(AB11), .out(lookuptable_3_out));
  Seven_Seg_Hex seven_seg_hex_4 (.d(lookuptable_4_out), .dp(pulldown_17_out));
  PullDown pulldown_17 (.out(pulldown_17_out));
  LookUpTable #(.Bits(4)) lookuptable_4 (.in0(PC8), .in1(PC9), .in2(PC10), .in3(PC11), .out(lookuptable_4_out));
  Button button_1 (.out(button_1_out));
  or or_1 (or_1_out, HALT, button_2_out);
  Button button_2 (.out(button_2_out));
  Button button_3 (.out(button_3_out));
  or or_2 (or_2_out, button_3_out, RESET);
  LED led_5 (.in(DB5));
  LED led_6 (.in(DB4));
  LED led_7 (.in(R5));
  LED led_8 (.in(R4));
  PullDown pulldown_18 (.out(AB15));
  PullDown pulldown_19 (.out(AB14));
  PullDown pulldown_20 (.out(AB13));
  PullDown pulldown_21 (.out(AB12));
  PullDown pulldown_22 (.out(AB11));
  PullDown pulldown_23 (.out(AB10));
  PullDown pulldown_24 (.out(AB9));
  PullDown pulldown_25 (.out(AB8));
  Seven_Seg_Hex seven_seg_hex_5 (.d(lookuptable_5_out), .dp(pulldown_26_out));
  LookUpTable #(.Bits(4)) lookuptable_5 (.in0(AB4), .in1(AB5), .in2(AB6), .in3(AB7), .out(lookuptable_5_out));
  Seven_Seg_Hex seven_seg_hex_6 (.d(lookuptable_6_out), .dp(pulldown_27_out));
  LookUpTable #(.Bits(4)) lookuptable_6 (.in0(PC4), .in1(PC5), .in2(PC6), .in3(PC7), .out(lookuptable_6_out));
  RS_FF_AS rs_ff_as_1 (.S(button_1_out), .R(or_1_out), .Q(rs_ff_as_1_q), .nQ(rs_ff_as_1_nq));
  not not_2 (CLR, or_2_out);
  LED led_9 (.in(DB3));
  LED led_10 (.in(DB2));
  LED led_11 (.in(R3));
  LED led_12 (.in(R2));
  Seven_Seg_Hex seven_seg_hex_7 (.d(lookuptable_7_out), .dp(pulldown_36_out));
  PullDown pulldown_26 (.out(pulldown_26_out));
  LookUpTable #(.Bits(4)) lookuptable_7 (.in0(AB0), .in1(AB1), .in2(AB2), .in3(AB3), .out(lookuptable_7_out));
  Seven_Seg_Hex seven_seg_hex_8 (.d(lookuptable_8_out), .dp(pulldown_37_out));
  PullDown pulldown_27 (.out(pulldown_27_out));
  LookUpTable #(.Bits(4)) lookuptable_8 (.in0(PC0), .in1(PC1), .in2(PC2), .in3(PC3), .out(lookuptable_8_out));
  Break break_1 (.brk(clk));
  LED led_13 (.in(DB1));
  LED led_14 (.in(DB0));
  LED led_15 (.in(R1));
  LED led_16 (.in(R0));
  PullDown pulldown_28 (.out(AB7));
  PullDown pulldown_29 (.out(AB6));
  PullDown pulldown_30 (.out(AB5));
  PullDown pulldown_31 (.out(AB4));
  PullDown pulldown_32 (.out(AB3));
  PullDown pulldown_33 (.out(AB2));
  PullDown pulldown_34 (.out(AB1));
  PullDown pulldown_35 (.out(AB0));
  PullDown pulldown_36 (.out(pulldown_36_out));
  PullDown pulldown_37 (.out(pulldown_37_out));
  and and_1 (CLK_t, clk, rs_ff_as_1_q);
  LED led_17 (.in(rs_ff_as_1_q));
  LED led_18 (.in(rs_ff_as_1_nq));
  PullDown pulldown_38 (.out(DB7));
  PullDown pulldown_39 (.out(DB6));
  PullDown pulldown_40 (.out(DB5));
  PullDown pulldown_41 (.out(DB4));
  PullDown pulldown_42 (.out(DB3));
  PullDown pulldown_43 (.out(DB2));
  PullDown pulldown_44 (.out(DB1));
  PullDown pulldown_45 (.out(DB0));
  _74373 _74373_1 (
    .pin1(B_IMM), .pin2(B0), .pin3(DB0), .pin4(DB1), .pin5(B1), .pin6(B2), .pin7(DB2), .pin8(DB3), .pin9(B3),
    .pin10(1'b0), .pin11(B_WE), .pin12(B4), .pin13(DB4), .pin14(DB5), .pin15(B5), .pin16(B6), .pin17(DB6),
    .pin18(DB7), .pin19(B7), .pin20(1'b1));
  _74373 _74373_2 (
    .pin1(R_RE), .pin2(DB0), .pin3(R0), .pin4(R1), .pin5(DB1), .pin6(DB2), .pin7(R2), .pin8(R3), .pin9(DB3),
    .pin10(1'b0), .pin11(R_WE), .pin12(DB4), .pin13(R4), .pin14(R5), .pin15(DB5), .pin16(DB6), .pin17(R6),
    .pin18(R7), .pin19(DB7), .pin20(1'b1));
  _74161 _74161_1 (
    .pin1(CLR), .pin2(CLK_t), .pin3(AB12), .pin4(AB13), .pin5(AB14), .pin6(AB15), .pin7(TIE2), .pin8(1'b0),
    .pin9(LD), .pin10(TIE2), .pin11(PC15), .pin12(PC14), .pin13(PC13), .pin14(PC12), .pin16(1'b1));  // open: pin15
  _74373 _74373_3 (
    .pin1(_74373_3_pin1), .pin2(AB8), .pin3(MAR8), .pin4(MAR9), .pin5(AB9), .pin6(AB10), .pin7(MAR10),
    .pin8(MAR11), .pin9(AB11), .pin10(1'b0), .pin11(MAR_WHI), .pin12(AB12), .pin13(MAR12), .pin14(MAR13),
    .pin15(AB13), .pin16(AB14), .pin17(MAR14), .pin18(MAR15), .pin19(AB15), .pin20(1'b1));
  not not_3 (_74373_3_pin1, iAB_MAR);
  _74157 _74157_1 (
    .pin1(MAR_AB_DB), .pin2(AB12), .pin3(DB4), .pin4(MAR12), .pin5(AB13), .pin6(DB5), .pin7(MAR13),
    .pin8(1'b0), .pin9(MAR14), .pin10(DB6), .pin11(AB14), .pin12(MAR15), .pin13(DB7), .pin14(AB15),
    .pin15(_74157_1_pin15), .pin16(1'b1));
  // A623308A a623308a_1: pin names not known; wires that end beside it: 1'b1, RAM_WE, AB12, AB7, AB8, AB6, AB9, AB5, AB11, AB4, RAM_RE, AB3, AB10, AB2, RAM_CE, AB1, DB7, AB0, DB0, DB1, DB2, 1'b0
  PullDown pulldown_46 (.out(_74157_1_pin15));
  _74161 _74161_2 (
    .pin1(CLR), .pin2(CLK_t), .pin3(AB8), .pin4(AB9), .pin5(AB10), .pin6(AB11), .pin7(TIE1), .pin8(1'b0),
    .pin9(LD), .pin10(TIE1), .pin11(PC11), .pin12(PC10), .pin13(PC9), .pin14(PC8), .pin15(TIE2), .pin16(1'b1));
  _74157 _74157_2 (
    .pin1(MAR_AB_DB), .pin2(AB8), .pin3(DB0), .pin4(MAR8), .pin5(AB9), .pin6(DB1), .pin7(MAR9), .pin8(1'b0),
    .pin9(MAR10), .pin10(DB2), .pin11(AB10), .pin12(MAR11), .pin13(DB3), .pin14(AB11),
    .pin15(_74157_2_pin15), .pin16(1'b1));
  _74373 _74373_4 (
    .pin1(_74373_4_pin1), .pin2(AB0), .pin3(MAR0), .pin4(MAR1), .pin5(AB1), .pin6(AB2), .pin7(MAR2),
    .pin8(MAR3), .pin9(AB3), .pin10(1'b0), .pin11(MAR_WLO), .pin12(AB4), .pin13(MAR4), .pin14(MAR5),
    .pin15(AB5), .pin16(AB6), .pin17(MAR6), .pin18(MAR7), .pin19(AB7), .pin20(1'b1));
  not not_4 (_74373_4_pin1, iAB_MAR);
  PullDown pulldown_47 (.out(_74157_2_pin15));
  _74245 _74245_1 (
    .pin1(_74245_1_pin1), .pin2(B0), .pin3(B1), .pin4(B2), .pin5(B3), .pin6(B4), .pin7(B5), .pin8(B6),
    .pin9(B7), .pin10(1'b0), .pin11(DB7), .pin12(DB6), .pin13(DB5), .pin14(DB4), .pin15(DB3), .pin16(DB2),
    .pin17(DB1), .pin18(DB0), .pin19(BtoDB), .pin20(1'b1));
  PullUp pullup_5 (.out(_74245_1_pin1));
  _74245 _74245_2 (
    .pin1(_74245_2_pin1), .pin2(AB8), .pin3(AB9), .pin4(AB10), .pin5(AB11), .pin6(AB12), .pin7(AB13),
    .pin8(AB14), .pin9(AB15), .pin10(1'b0), .pin11(DB7), .pin12(DB6), .pin13(DB5), .pin14(DB4), .pin15(DB3),
    .pin16(DB2), .pin17(DB1), .pin18(DB0), .pin19(ABHtoDB), .pin20(1'b1));
  PullUp pullup_6 (.out(_74245_2_pin1));
  _74161 _74161_3 (
    .pin1(CLR), .pin2(CLK_t), .pin3(AB4), .pin4(AB5), .pin5(AB6), .pin6(AB7), .pin7(TIE0), .pin8(1'b0),
    .pin9(LD), .pin10(TIE0), .pin11(PC7), .pin12(PC6), .pin13(PC5), .pin14(PC4), .pin15(TIE1), .pin16(1'b1));
  PullDown pulldown_48 (.out(pulldown_48_out));
  _74157 _74157_3 (
    .pin1(MAR_AB_DB), .pin2(AB4), .pin3(DB4), .pin4(MAR4), .pin5(AB5), .pin6(DB5), .pin7(MAR5), .pin8(1'b0),
    .pin9(MAR6), .pin10(DB6), .pin11(AB6), .pin12(MAR7), .pin13(DB7), .pin14(AB7), .pin15(pulldown_48_out),
    .pin16(1'b1));
  LookUpTable #(.Bits(10)) lookuptable_9 (
    .in0(OPC0), .in1(OPC1), .in2(OPC2), .in3(OPC3), .in4(OPC5), .in5(OPC5),
    .out({lookuptable_9_out[9:7], R_WE, lookuptable_9_out[5:4], B_WE, lookuptable_9_out[2:0]}));
  LookUpTable #(.Bits(10)) lookuptable_10 (
    .in0(OPC0), .in1(OPC1), .in2(OPC2), .in3(OPC3), .in4(OPC5), .in5(OPC5),
    .out({lookuptable_10_out[9:7], EP_DIR, lookuptable_10_out[5], BGT, BEQ, BLT, JCF, JMP}));
  not not_5 (RAM_CE, lookuptable_9_out[0]);
  not not_6 (RAM_RE, lookuptable_9_out[1]);
  not not_7 (RAM_WE, lookuptable_9_out[2]);
  not not_8 (BtoDB, lookuptable_9_out[4]);
  not not_9 (R_RE, lookuptable_9_out[5]);
  not not_10 (EP_OE, lookuptable_10_out[5]);
  not not_11 (EPS, lookuptable_10_out[7]);
  _74161 _74161_4 (
    .pin1(CLR), .pin2(CLK_t), .pin3(AB0), .pin4(AB1), .pin5(AB2), .pin6(AB3), .pin7(_74161_4_pin7),
    .pin8(1'b0), .pin9(LD), .pin10(_74161_4_pin10), .pin11(PC3), .pin12(PC2), .pin13(PC1), .pin14(PC0),
    .pin15(TIE0), .pin16(1'b1));
  PullDown pulldown_49 (.out(pulldown_49_out));
  _74157 _74157_4 (
    .pin1(MAR_AB_DB), .pin2(AB0), .pin3(DB0), .pin4(MAR0), .pin5(AB1), .pin6(DB1), .pin7(MAR1), .pin8(1'b0),
    .pin9(MAR2), .pin10(DB2), .pin11(AB2), .pin12(MAR3), .pin13(DB3), .pin14(AB3), .pin15(pulldown_49_out),
    .pin16(1'b1));
  _74245 _74245_3 (
    .pin1(_74245_3_pin1), .pin2(AB0), .pin3(AB1), .pin4(AB2), .pin5(AB3), .pin6(AB4), .pin7(AB5), .pin8(AB6),
    .pin9(AB7), .pin10(1'b0), .pin11(DB7), .pin12(DB6), .pin13(DB5), .pin14(DB4), .pin15(DB3), .pin16(DB2),
    .pin17(DB1), .pin18(DB0), .pin19(ABLtoDB), .pin20(1'b1));
  PullUp pullup_7 (.out(_74245_3_pin1));
  LookUpTable #(.Bits(10)) lookuptable_11 (
    .in0(OPC0), .in1(OPC1), .in2(OPC2), .in3(OPC3), .in4(OPC5), .in5(OPC5),
    .out({lookuptable_11_out[9:4], MAR_WHI, MAR_WLO, lookuptable_11_out[1:0]}));
  LookUpTable #(.Bits(10)) lookuptable_12 (
    .in0(OPC0), .in1(OPC1), .in2(OPC2), .in3(OPC3), .in4(OPC5), .in5(OPC5),
    .out({lookuptable_12_out[9], CLR_CF_BF, RESET, HALT, lookuptable_12_out[5], XOR_P1, AND_OR, lookuptable_12_out[2], ADD_SUB, lookuptable_12_out[0]}));
  PullUp pullup_8 (.out(_74161_4_pin10));
  PullUp pullup_9 (.out(_74161_4_pin7));
  not not_12 (ABLtoDB, lookuptable_11_out[0]);
  not not_13 (ABHtoDB, lookuptable_11_out[1]);
  not not_14 (MAR_AB_DB, lookuptable_11_out[4]);
  not not_15 (ADDER, lookuptable_12_out[0]);
  not not_16 (LOGIC, lookuptable_12_out[2]);
  not not_17 (P1_LOGIC, lookuptable_12_out[5]);
  LED led_19 (.in(B_eq));
  LED led_20 (.in(B_lt));
  LED led_21 (.in(B_gt));
  LED led_22 (.in(CF_BF));
  LED led_23 (.in(JMP));
  _74245 _74245_4 (
    .pin1(EP_DIR), .pin2(DB0), .pin3(DB1), .pin4(DB2), .pin5(DB3), .pin6(DB4), .pin7(DB5), .pin8(DB6),
    .pin9(DB7), .pin10(1'b0), .pin11(EP7), .pin12(EP6), .pin13(EP5), .pin14(EP4), .pin15(EP3), .pin16(EP2),
    .pin17(EP1), .pin18(EP0), .pin19(EP_OE), .pin20(1'b1));
  _7485 _7485_1 (
    .pin1(B7), .pin2(lt), .pin3(eq), .pin4(gt), .pin5(CMP_gt), .pin6(CMP_eq), .pin7(CMP_lt), .pin8(1'b0),
    .pin9(B4), .pin10(DB4), .pin11(B5), .pin12(DB5), .pin13(DB6), .pin14(B6), .pin15(DB7), .pin16(1'b1));
  PullDown pulldown_50 (.out(pulldown_50_out));
  _74157 _74157_5 (
    .pin1(XOR_P1), .pin2(ADD_SUB), .pin3(DB4), .pin4(XOR4), .pin5(ADD_SUB), .pin6(DB5), .pin7(XOR5),
    .pin8(1'b0), .pin9(XOR6), .pin10(DB6), .pin11(ADD_SUB), .pin12(XOR7), .pin13(DB7), .pin14(ADD_SUB),
    .pin15(pulldown_50_out), .pin16(1'b1));
  _7408 _7408_1 (
    .pin1(ANDOR4), .pin2(B4), .pin3(AND4), .pin4(ANDOR5), .pin5(B5), .pin6(AND5), .pin7(1'b0), .pin8(AND6),
    .pin9(ANDOR6), .pin10(B6), .pin11(AND7), .pin12(ANDOR7), .pin13(B7), .pin14(1'b1));
  PullDown pulldown_51 (.out(pulldown_51_out));
  _74157 _74157_6 (
    .pin1(AND_OR), .pin2(AND4), .pin3(OR4), .pin4(XORB4), .pin5(AND5), .pin6(OR5), .pin7(XORB5), .pin8(1'b0),
    .pin9(XORB6), .pin10(OR6), .pin11(AND6), .pin12(XORB7), .pin13(OR7), .pin14(AND7),
    .pin15(pulldown_51_out), .pin16(1'b1));
  _74245 _74245_5 (
    .pin1(_74245_5_pin1), .pin2(LOG0), .pin3(LOG1), .pin4(LOG2), .pin5(LOG3), .pin6(LOG4), .pin7(LOG5),
    .pin8(LOG6), .pin9(LOG7), .pin10(1'b0), .pin11(R7), .pin12(R6), .pin13(R5), .pin14(R4), .pin15(R3),
    .pin16(R2), .pin17(R1), .pin18(R0), .pin19(LOGIC), .pin20(1'b1));
  PullUp pullup_10 (.out(_74245_5_pin1));
  _74245 _74245_6 (
    .pin1(_74245_6_pin1), .pin2(SUM0), .pin3(SUM1), .pin4(SUM2), .pin5(SUM3), .pin6(SUM4), .pin7(SUM5),
    .pin8(SUM6), .pin9(SUM7), .pin10(1'b0), .pin11(R7), .pin12(R6), .pin13(R5), .pin14(R4), .pin15(R3),
    .pin16(R2), .pin17(R1), .pin18(R0), .pin19(ADDER), .pin20(1'b1));
  PullUp pullup_11 (.out(_74245_6_pin1));
  not not_18 (not_18_out, EP_OE);
  and and_2 (and_2_out, EP_DIR, not_18_out);
  Terminal terminal_1 (.D({EP7, EP6, EP5, EP4, EP3, EP2, EP1, EP0}), .C(CLK_t), .en(and_2_out));
  _7485 _7485_2 (
    .pin1(B3), .pin2(_7485_2_pin2), .pin3(_7485_2_pin3), .pin4(_7485_2_pin4), .pin5(gt), .pin6(eq),
    .pin7(lt), .pin8(1'b0), .pin9(B0), .pin10(DB0), .pin11(B1), .pin12(DB1), .pin13(DB2), .pin14(B2),
    .pin15(DB3), .pin16(1'b1));
  _74157 _74157_7 (
    .pin1(XOR_P1), .pin2(ADD_SUB), .pin3(DB0), .pin4(XOR0), .pin5(ADD_SUB), .pin6(DB1), .pin7(XOR1),
    .pin8(1'b0), .pin9(XOR2), .pin10(DB2), .pin11(ADD_SUB), .pin12(XOR3), .pin13(DB3), .pin14(ADD_SUB),
    .pin15(_74157_7_pin15), .pin16(1'b1));
  _7408 _7408_2 (
    .pin1(ANDOR0), .pin2(B0), .pin3(AND0), .pin4(ANDOR1), .pin5(B1), .pin6(AND1), .pin7(1'b0), .pin8(AND2),
    .pin9(ANDOR2), .pin10(B2), .pin11(AND3), .pin12(ANDOR3), .pin13(B3), .pin14(1'b1));
  _74157 _74157_8 (
    .pin1(AND_OR), .pin2(AND0), .pin3(OR0), .pin4(XORB0), .pin5(AND1), .pin6(OR1), .pin7(XORB1), .pin8(1'b0),
    .pin9(XORB2), .pin10(OR2), .pin11(AND2), .pin12(XORB3), .pin13(OR3), .pin14(AND3),
    .pin15(_74157_8_pin15), .pin16(1'b1));
  PullDown pulldown_52 (.out(_7485_2_pin2));
  PullUp pullup_12 (.out(_7485_2_pin3));
  PullDown pulldown_53 (.out(_74157_7_pin15));
  PullDown pulldown_54 (.out(_74157_8_pin15));
  _7486 _7486_1 (
    .pin1(XOR4), .pin2(XORB4), .pin3(LOG4), .pin4(XOR5), .pin5(XORB5), .pin6(LOG5), .pin7(1'b0), .pin8(LOG6),
    .pin9(XOR6), .pin10(XORB6), .pin11(LOG7), .pin12(XOR7), .pin13(XORB7), .pin14(1'b1));
  _74283 _74283_1 (
    .pin1(SUM5), .pin2(LOG5), .pin3(DB5), .pin4(SUM4), .pin5(DB4), .pin6(LOG4), .pin7(CO_CI), .pin8(1'b0),
    .pin9(CF), .pin10(SUM7), .pin11(LOG7), .pin12(DB7), .pin13(SUM6), .pin14(DB6), .pin15(LOG6), .pin16(1'b1));
  PullDown pulldown_55 (.out(_7485_2_pin4));
  _74245 _74245_7 (
    .pin1(_74245_7_pin1), .pin2(DB0), .pin3(DB1), .pin4(DB2), .pin5(DB3), .pin6(DB4), .pin7(DB5), .pin8(DB6),
    .pin9(DB7), .pin10(1'b0), .pin11(_74245_7_pin11), .pin12(_74245_7_pin12), .pin13(_74245_7_pin13),
    .pin14(_74245_7_pin14), .pin15(_74245_7_pin15), .pin16(_74245_7_pin16), .pin17(_74245_7_pin17),
    .pin18(AV), .pin19(EPS), .pin20(1'b1));
  PullDown pulldown_56 (.out(_74245_7_pin1));
  not not_19 (not_19_out, EP_DIR);
  not not_20 (not_20_out, EP_OE);
  _7432 _7432_1 (
    .pin1(ANDOR4), .pin2(B4), .pin3(OR4), .pin4(ANDOR5), .pin5(B5), .pin6(OR5), .pin7(1'b0), .pin8(OR6),
    .pin9(ANDOR6), .pin10(B6), .pin11(OR7), .pin12(ANDOR7), .pin13(B7), .pin14(1'b1));
  and and_3 (and_3_out, not_19_out, not_20_out);
  _7408 _7408_3 (
    .pin1(CMP_gt), .pin2(BGT), .pin3(B_gt), .pin4(CMP_eq), .pin5(BEQ), .pin6(B_eq), .pin7(1'b0), .pin8(B_lt),
    .pin9(CMP_lt), .pin10(BLT), .pin11(CFlag), .pin12(JCF), .pin13(CF_BF), .pin14(1'b1));
  _74245 _74245_8 (
    .pin1(_74245_8_pin1), .pin2(DB0), .pin3(DB1), .pin4(DB2), .pin5(DB3), .pin6(DB4), .pin7(DB5), .pin8(DB6),
    .pin9(DB7), .pin10(1'b0), .pin11(ANDOR7), .pin12(ANDOR6), .pin13(ANDOR5), .pin14(ANDOR4), .pin15(ANDOR3),
    .pin16(ANDOR2), .pin17(ANDOR1), .pin18(ANDOR0), .pin19(P1_LOGIC), .pin20(1'b1));
  PullUp pullup_13 (.out(_74245_8_pin1));
  PullDown pulldown_57 (.out(_74245_7_pin17));
  PullDown pulldown_58 (.out(_74245_7_pin16));
  _7486 _7486_2 (
    .pin1(XOR0), .pin2(XORB0), .pin3(LOG0), .pin4(XOR1), .pin5(XORB1), .pin6(LOG1), .pin7(1'b0), .pin8(LOG2),
    .pin9(XOR2), .pin10(XORB2), .pin11(LOG3), .pin12(XOR3), .pin13(XORB3), .pin14(1'b1));
  _74283 _74283_2 (
    .pin1(SUM1), .pin2(LOG1), .pin3(DB1), .pin4(SUM0), .pin5(DB0), .pin6(LOG0), .pin7(ADD_SUB), .pin8(1'b0),
    .pin9(CO_CI), .pin10(SUM3), .pin11(LOG3), .pin12(DB3), .pin13(SUM2), .pin14(DB2), .pin15(LOG2),
    .pin16(1'b1));
  PullDown pulldown_59 (.out(_74245_7_pin15));
  PullDown pulldown_60 (.out(_74245_7_pin14));
  Keyboard keyboard_1 (.C(CLK_t), .en(and_3_out), .D({keyboard_1_d, EP7, EP6, EP5, EP4, EP3, EP2, EP1, EP0}), .av(AV));
  PullDown pulldown_61 (.out(_74245_7_pin13));
  PullDown pulldown_62 (.out(_74245_7_pin12));
  _7432 _7432_2 (
    .pin1(ANDOR0), .pin2(B0), .pin3(OR0), .pin4(ANDOR1), .pin5(B1), .pin6(OR1), .pin7(1'b0), .pin8(OR2),
    .pin9(ANDOR2), .pin10(B2), .pin11(OR3), .pin12(ANDOR3), .pin13(B3), .pin14(1'b1));
  PullDown pulldown_63 (.out(_74245_7_pin11));
  _74260 _74260_1 (
    .pin1(B_gt), .pin2(B_eq), .pin3(B_lt), .pin4(_74260_1_pin4), .pin5(LD), .pin7(1'b0),
    .pin8(_74260_1_pin8), .pin9(_74260_1_pin9), .pin10(_74260_1_pin10), .pin11(_74260_1_pin11),
    .pin12(CFlag), .pin13(JMP), .pin14(1'b1));  // open: pin6
  xor xor_1 (xor_1_out, CF, ADD_SUB);
  PullDown pulldown_64 (.out(_74260_1_pin10));
  PullDown pulldown_65 (.out(_74260_1_pin11));
  PullDown pulldown_66 (.out(_74260_1_pin4));
  PullDown pulldown_67 (.out(_74260_1_pin9));
  PullDown pulldown_68 (.out(_74260_1_pin8));
  RS_FF_AS rs_ff_as_2 (.S(xor_1_out), .R(CLR_CF_BF), .Q(CF_BF));  // open: nQ

  // Notes on the sheet:
  //   AB HI
  //   AB LO
  //   OPCODE
  //   IMM
  //   Program
  //   Store
  //   contents of lookuptable_1 (hex, n*v repeats v):
  //   0,1,2,3,4,5,6,7,8,9,a,b,c,d,e,f
  //   PROGRAM COUNTER
  //   contents of lookuptable_2 (hex, n*v repeats v):
  //   0,1,2,3,4,5,6,7,8,9,a,b,c,d,e,f
  //   CLOCK
  //   RUN
  //   HALT
  //   RESET
  //   ADDRESS BUS
  //   contents of lookuptable_3 (hex, n*v repeats v):
  //   0,1,2,3,4,5,6,7,8,9,a,b,c,d,e,f
  //   contents of lookuptable_4 (hex, n*v repeats v):
  //   0,1,2,3,4,5,6,7,8,9,a,b,c,d,e,f
  //   contents of lookuptable_5 (hex, n*v repeats v):
  //   0,1,2,3,4,5,6,7,8,9,a,b,c,d,e,f
  //   contents of lookuptable_6 (hex, n*v repeats v):
  //   0,1,2,3,4,5,6,7,8,9,a,b,c,d,e,f
  //   contents of lookuptable_7 (hex, n*v repeats v):
  //   0,1,2,3,4,5,6,7,8,9,a,b,c,d,e,f
  //   contents of lookuptable_8 (hex, n*v repeats v):
  //   0,1,2,3,4,5,6,7,8,9,a,b,c,d,e,f
  //   B
  //   R
  //   PC
  //   MAR
  //   DB/AB 
  //   to 
  //   MAR
  //   RAM
  //   B
  //   to
  //   DB
  //   AB L|H
  //   to
  //   DB
  //   contents of lookuptable_9 (hex, n*v repeats v):
  //   0,0,0,25,15,5,0,3,3,0,0,0,20,20,20,43
  //   contents of lookuptable_10 (hex, n*v repeats v):
  //   0,0,0,0,0,20,0,0,60,1,2,0,4,8,10
  //   contents of lookuptable_11 (hex, n*v repeats v):
  //   0,0,0,0,0,0,c
  //   contents of lookuptable_12 (hex, n*v repeats v):
  //   0,40,80,0,0,0,0,0,0,0,0,100,0,0,0,9
  //   EP
  //   EPS
  //   contents of Byte 4 (hex, n*v repeats v):
  //   0,0,0,0,0,0,0,0,0,0,0,0,0,0,0,0,0,0,0,0,0,0,0,0,0,0,0,0,0,0,0,0,0,0,0,0,0,0,0,0,0, 0,0,0,0,
  //   0,0,0,0,0,0,0,0,0,0,0,0,0,0,0,0,0,0,0,0,0,0,0,0,0,0,0,0,0,0,0,0,0,0,0,0,0, 0,0,0,0,0,0,0,0,
  //   0,0,0,0,0,0,0,0,0,0,0,0,0,0,0,0,0,0,0,0,0,0,0,0,0,0,0,0,0,0,0,0,0, 0,0,0,0,0,0,0,0,0,0,0,0,
  //   0,0,0,0,0,0,0,0,0,0,0,0,0,0,0,0,0,0,0,0,0,0,0,0,0,0,0,0,0, 0,0,0,0,0,0,0,0,0,0,0,0,0,0,0,0,
  //   0,0,0,0,0,0,0,0,0,0,0,0,0,0,0,0,0,0,0,0,0,0,0,0,0, 0,0,0,0,0,0,0,0,0,0,0,0,0,0,0,0,0,0,0,0,
  //   0,0,0,0,0,0,0,0,0,0,0,0,0,0,0,0,0,0,0,0,0, 0,0,0,0,0,0,0,0,0,0,0,0,0,0,0,0,0,0,0,0,0,0,0,0,
  //   0,0,0,0,0,0,0,0,0,0,0,0,0,0,0,0,0, 0,0,0,0,0,0,0,0,0,0,0,0,0,0,0,0,0,0,0,0,0,0,0,0,0,0,0,0,
  //   0,0,0,0,0,0,0,0,0,0,0,0,0, 0,0,0,0,1
  //   contents of Byte 3 (hex, n*v repeats v):
  //   7,10,5,12,0,11,0,10,11,12,1
  //   contents of Byte 2 (hex, n*v repeats v):
  //   0,0,10,0,0,0,0,11,47,42
  //   contents of Byte 1 (hex, n*v repeats v):
  //   9,4f,4e,8,1,8,1,44,44,44,9
endmodule
